// Logisim project 3chiglue.circ as structural Verilog: 1 circuit, main circuit main
module main (
  input  [3:0] A13,
  input  [3:0] in_2,
  input  [3:0] in_3,
  input  [3:0] in_4,
  input  A15,
  input  A14,
  input  in_7,
  input  A12,
  input  in_9,
  input  in_10,
  input  in_11,
  input  in_12,
  input  in_13,
  input  in_14,
  input  in_15,
  input  in_16,
  input  in_17,
  input  in_18,
  input  in_19,
  input  A0
);

  wire ACIA_out, BCD_out, nand_1_out, nand_2_out, nand_3_out, nand_4_out, nand_5_out, nand_6_out, nand_8_out,
       nand_9_out, not_1_out, not_2_out, not_3_out, VIA1_out, VIA2_out;
  wire [1:1] nand_7_out;
  wire [3:3] clock_1_out;

  nand nand_1 (nand_1_out, A15, A15);
  Hex_Digit_Display hex_digit_display_1 (.value(A13));  // open: dp
  Clock clock_1 (.out(clock_1_out[3]));
  nand nand_2 (nand_2_out, nand_1_out, clock_1_out[3]);
  // Probe on nand_2_out
  Hex_Digit_Display hex_digit_display_2 (.value(in_2));  // open: dp
  nand nand_3 (nand_3_out, A15, A14);
  // Probe on nand_3_out
  Hex_Digit_Display hex_digit_display_3 (.value(in_3));  // open: dp
  Hex_Digit_Display hex_digit_display_4 (.value(in_4));  // open: dp
  nand nand_4 (nand_4_out, A14, A14);
  nand nand_5 (nand_5_out, A15, nand_4_out);
  nand nand_6 (nand_6_out, nand_5_out, nand_5_out);
  nand nand_7 (nand_7_out[1], nand_6_out, in_7);
  PLA #(.out_width(1), .\table ("00 1\n11 1\n10 1\n01 0")) VIA1 (.in({nand_7_out[1], in_16}), .out(VIA1_out));
  PLA #(.in_width(4), .out_width(1), .\table ("0000 1\n0001 1\n0010 1\n0011 1\n0100 1\n0101 1\n0110 1\n0111 1\n1100 0\n1001 1\n1010 1\n1011 1\n1100 1\n1101 1\n1110 1\n1111 1\n1000 1")) BCD (
    .in({clock_1_out[3], A15, A14, in_7}), .out(BCD_out));
  // Probe on VIA1_out
  PLA #(.out_width(1), .\table ("00 1\n11 1\n01 0\n10 1")) VIA2 (.in({nand_7_out[1], in_15}), .out(VIA2_out));
  // Probe on VIA2_out
  not not_1 (not_1_out, BCD_out);
  not not_2 (not_2_out, A12);
  not not_3 (not_3_out, BCD_out);
  PLA #(.out_width(1), .\table ("00 1\n11 1\n01 0\n10 1")) ACIA (.in({nand_7_out[1], in_14}), .out(ACIA_out));
  nand nand_8 (nand_8_out, A12, not_1_out);
  // Probe on nand_8_out
  // Probe on nand_9_out
  nand nand_9 (nand_9_out, not_2_out, not_3_out);
  // Probe on ACIA_out

  // Notes on the sheet:
  //   RAM
  //   ROM
  //   VIDEO
  //   color memory
  //   character memory
endmodule
